# Fritzing sketch microbit-Potentiometers-and-speakers circuit (saved by Fritzing 0.9.3b)

parts:
  Mod1 = Microbit
  SPKR1 = Speaker0.5W8Ohm

nets:
  N1: Mod1.P0, SPKR1.pin2
  N2: Mod1.GND, SPKR1.pin1

custom parts:
  Microbit: BBC Microbit Fritzing part. May 2019 expanded to include schematic and pcb views as well as breadboard. PCB view assumes an Adafruit PRODUCT ID: 3342 2x40 Right Angle through hole edge connector (although others will probably work as well). The pcb svg is custom (see forum article http://forum.fritzing.org/t/making-edge-connectors-and-both-side-smd-parts/7287 for an explaination if you need to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
  Speaker0.5W8Ohm: A small audio speaker that is ideal for radio and amplifier projects and is small enough to fit in robot projects.
